// Logisim project cpu.circ as structural Verilog: 1 circuit, main circuit cpu
module cpu (
  input  clk,
  input  [31:0] Instruction,
  input  [31:0] MemReadData,
  output [31:0] MemAddress,
  output [31:0] ProgramCounter,
  output [31:0] ra,
  output [31:0] sp,
  output [31:0] t0,
  output [31:0] t1,
  output [31:0] t2,
  output [31:0] s0,
  output [31:0] s1,
  output [31:0] a0,
  output [3:0] MemWriteMask,
  output [31:0] MemWriteData
);

  wire ASel, BSel, RegWEn;
  wire [2:0] ImmSel;
  wire [3:0] ALUSel;
  wire [31:0] adder_1_out, ALUResult, Immediate, InputA, InputB, RegReadData1, RegReadData2;

  Register #(.width(32)) PC (.D(adder_1_out), .clk(clk), .Q(ProgramCounter));  // open: en, clr
  Adder #(.width(32)) adder_1 (.a(ProgramCounter), .b(32'h4), .out(adder_1_out));  // open: cin, cout
  imm_gen imm_gen_1 (.Instruction(Instruction), .ImmSel(ImmSel), .Immediate(Immediate));
  control_logic control_logic_1 (
    .RegWEn(RegWEn), .ImmSel(ImmSel), .ASel(ASel), .BSel(BSel), .ALUSel(ALUSel), .Instruction(Instruction));  // open: PCSel, BrUn, MemWEn, WBSel, BrEq, BrLt
  regfile regfile_1 (
    .ReadReg1(Instruction[19:15]), .ReadReg2(Instruction[24:20]), .WriteReg(Instruction[11:7]),
    .RegWriteData(ALUResult), .RegWEn(RegWEn), .clk(clk), .ra(ra), .sp(sp), .t0(t0), .t1(t1), .t2(t2),
    .s0(s0), .s1(s1), .a0(a0), .RegReadData1(RegReadData1), .RegReadData2(RegReadData2));
  Multiplexer #(.width(32)) multiplexer_1 (.in0(RegReadData1), .in1(ProgramCounter), .out(InputA), .sel(ASel));
  Multiplexer #(.width(32)) multiplexer_2 (.in0(RegReadData2), .in1(Immediate), .out(InputB), .sel(BSel));
  alu alu_1 (.ALUResult(ALUResult), .A(InputA), .B(InputB), .ALUSel(ALUSel));
  // branch_comp branch_comp_1: pin names not known
  // partial_store partial_store_1: pin names not known
  // partial_load partial_load_1: pin names not known

  // Other names for the same wires on the sheet: WriteReg[4:0] = Instruction[11:7];
  //   ReadReg1[4:0] = Instruction[19:15]; ReadReg2[4:0] = Instruction[24:20]

  // Notes on the sheet:
  //   To IMEM
  //   IMEM (do **NOT** move this)
  //   From IMEM
  //   Inputs/Outputs for testing. Do **NOT** move these.
  //   It is OK to move the PC, RegFile, ALU, MEM, Branch Comp, Imm Gen, Partial Load, Partial Store and Control Logic to wherever is most convenient for you when constructing your CPU, and to delete this text
  //   To DMEM
  //   DMEM (do **NOT** move this)
  //   From DMEM
endmodule
